# Fritzing sketch sensground_sketch (saved by Fritzing 0.9.3b)
breadboards: 1

parts:
  Componente1 = Arduino Uno (Rev3)
  Componente3 = FC-28 Soil Hygrometer Module - Probe
  Componente4 = FC-28 Soil Hygrometer Module
  JACK1 = 2.1mm Barrel Jack with Terminal Block
  VALVE1 = Plastic Solenoid Valve
  1_Channel_Relay1 = 1 Channel Power Relay

nets:
  N1: Componente1.A0, Componente4.AO
  N2: Componente1.D8, 1_Channel_Relay1.GND
  N3: Componente1.GND, Componente4.DO, 1_Channel_Relay1.IN
  VCC: Componente1.5V, Componente1.VIN, Componente4.VCC, 1_Channel_Relay1.VCC
  N4: Componente3.POS, Componente4.POS
  N5: Componente3.NEG, Componente4.NEG
  N6: JACK1.POS, 1_Channel_Relay1.COM
  N7: JACK1.NEG, VALVE1.no_name_yet#1
  N8: VALVE1.no_name_yet#2, 1_Channel_Relay1.NO

custom parts:
  FC-28 Soil Hygrometer Module - Probe: The FC-28 is a soil hygrometer module that uses the Texas Instruments LM393 comparator chip to provide an analog measurement of soil humidity.
  FC-28 Soil Hygrometer Module: The FC-28 is a soil hygrometer module that uses the Texas Instruments LM393 comparator chip to provide an analog measurement of soil humidity. The digital output is high when soil moisture is over a certain threshold, as determined by adjusting the potentiometer.
  1 Channel Power Relay: A 1 channel power relay. The module operates at 5V.

// code stored in the sketch: sensground.ino
// ===== SOIL LEVEL MOISTURE RANGE =====
// =====================================
#define L1 169
#define L2 340
#define L3 511
#define L4 682
#define L5 853

// ===== HARDWARE MAPPING =====
// ============================
//relay signalevel for valve
int valve = 8;

// ===== INITIAL LEVEL SETTINGS =====
// ==================================
void setup() {
  Serial.begin(9600);
  
  //declares valve as output
  pinMode(valve, OUTPUT);
}

// ===== LOOP INFINITO =====
// =========================
void loop() {
  //sensor reading on pin A0 and storage in SensorValue
  int sensorValue = analogRead(A0);

  //print sensor level
  Serial.print(" Nivel de umidade: ");
  Serial.println(sensorValue);

  //identifies humidity level 0
  if(sensorValue > 0 && sensorValue < L1) {
    Serial.println(" Status: Solo TOTALMENTE UMIDO!\n");

    //turn off valve
    digitalWrite(valve,HIGH);
  }
  //identifies humidity level 1
  else if(sensorValue > L1 && sensorValue < L2) {
    Serial.println(" Status: Umidade MEDIA!\n");

    //turn off valve
    digitalWrite(valve,HIGH);
    delay(1000);
  }
  //identifies humidity level 2
  else if(sensorValue > L2 && sensorValue < L3) {
    Serial.println(" Status: Umidade MINIMA!\n");

    //turn off valve
    digitalWrite(valve,HIGH);
    delay(1000);
  }
  //identifies humidity level 3
  else if(sensorValue > L3 && sensorValue < L4) {
    Serial.println(" Status: Solo SECANDO!\n PRONTO PARA INICIAR IRRIGACAO!\n");

    //turn off valve
    digitalWrite(valve,HIGH);
    delay(1000);
  }
  //identifies humidity level 4
  else if(sensorValue > L4 && sensorValue < L5) {
    Serial.println(" Status: Solo QUASE SECO!\n IRRIGANDO!!!\n");

    //turn on valve
    digitalWrite(valve,LOW);
    delay(1000);
  }
  //identifies humidity level 5
  else if(sensorValue > L5 && sensorValue < 1024) {
    Serial.println(" Status: ATENCAO!!! Solo SECO!\n IRRIGANDO!!!\n");

    //turn on valve
    digitalWrite(valve,LOW);
    delay(1000);
  }
  delay(800);
}
